# Fritzing sketch Untitled Sketch (saved by Fritzing 1.0.6)
breadboards: 2

parts:
  Componente1 = Arduino Mega ADK (Rev3)
  R4 = Rotary Potentiometer (Large) [maximum_resistance=1kΩ knob_status=50% power=0.5W package=THT]
  S1 = Pushbutton [package="[SMD]"]
  S2 = Pushbutton [package="[SMD]"]
  S3 = Pushbutton [package="[SMD]"]
  S4 = Pushbutton [package="[SMD]"]
  S5 = Pushbutton [package="[SMD]"]
  S6 = Pushbutton [package="[SMD]"]
  LCD1 = LCD screen
  R5 = Rotary Potentiometer (Large) [maximum_resistance=100kΩ knob_status=50% power=0.5W package=THT]
  R6 = Rotary Potentiometer (Large) [maximum_resistance=1kΩ knob_status=50% power=0.5W package=THT]
  R7 = Rotary Potentiometer (Large) [maximum_resistance=1kΩ knob_status=50% power=0.5W package=THT]
  R8 = Rotary Potentiometer (Large) [maximum_resistance=1kΩ knob_status=50% power=0.5W package=THT]

nets:
  N1: Componente1.A0, R8.wiper
  N2: Componente1.A1, R7.wiper
  N3: Componente1.A2, R6.wiper
  N4: Componente1.A3, R4.wiper
  N5: Componente1.D8_PWM, LCD1.E
  5V: Componente1.5V, R4.leg2, LCD1.VDD, LCD1.LED+, R5.leg2, R6.leg2, R7.leg2, R8.leg2
  GND: Componente1.GND, R4.leg1, LCD1.VSS, LCD1.R/W, LCD1.LED-, R5.leg1, R6.leg1, R7.leg1, R8.leg1
  N6: Componente1.D3_PWM, LCD1.DB7
  N7: Componente1.D4_PWM, LCD1.DB6
  N8: Componente1.D5_PWM, LCD1.DB5
  N9: Componente1.D6_PWM, LCD1.DB4
  N10: Componente1.D7_PWM, LCD1.RS
  N11: S1.Pin_1, S1.Pin_2
  N12: S1.Pin_3, S1.Pin_4
  N13: S2.Pin_1, S2.Pin_2
  N14: S2.Pin_3, S2.Pin_4
  N15: S3.Pin_1, S3.Pin_2
  N16: S3.Pin_3, S3.Pin_4
  N17: S4.Pin_1, S4.Pin_2
  N18: S4.Pin_3, S4.Pin_4
  N19: S5.Pin_1, S5.Pin_2
  N20: S5.Pin_3, S5.Pin_4
  N21: S6.Pin_1, S6.Pin_2
  N22: S6.Pin_3, S6.Pin_4
  N23: LCD1.V0, R5.wiper
